# Fritzing sketch Abeillez_Interupteur (saved by Fritzing 0.9.3b)

parts:
  Composant1 = Solar Cell
  Solar_Charger_Liporider_-_Seeed_Studio1 = Solar Charger Liporider - Seeed Studio
  Composant2 = Arduino MKR WAN 1310
  R1 = Resistor [tolerance=±5% resistance=1k package=THT]
  R2 = Resistor [tolerance=±5% resistance=1k package=THT]
  Int1 = Interrupteur à levier - 2 pins [package=THT]
  DHT1 = DHT11 Humitidy and Temperature Sensor
  DHT2 = DHT11 Humitidy and Temperature Sensor
  DS1 = DS18B20 1-Wire Temperature Sensor Probe Cable
  DS2 = DS18B20 1-Wire Temperature Sensor Probe Cable
  Composant3 = HX711 Weighing Sensor Module
  R3 = Resistor [tolerance=±5% resistance=220 package="0805 [SMD]"]
  LED1 = smd LED [color="Red (633nm)" package="1206 [SMD]"]
  Load_Cell1 = Load Cell - Red/white/black/green
  U1 = LIPO-2000mAh [package=lipo-2000]

nets:
  N1: Composant1.-, Solar_Charger_Liporider_-_Seeed_Studio1.nessun_nome#6
  N2: Solar_Charger_Liporider_-_Seeed_Studio1.nessun_nome#1, Int1.pin2, U1.+
  N3: Composant2.D0, R3.Pin_0
  N4: Composant2.D1, Composant3.DO/RX
  GND: Composant2.GND, R1.Pin_1, DHT1.GND, DHT2.GND, DS1.GND, DS2.GND, Composant3.GND, LED1.anode
  N5: Composant2.D2, Composant3.CK/TX
  N6: Composant2.D3~, DS1.DQ, DS2.DQ
  N7: Composant2.A1, DHT1.DATA
  N8: Composant2.A0, DHT2.DATA
  VDD: Composant2.+3V3, DHT1.VDD, DHT2.VDD, DS1.VDD, DS2.VDD, Composant3.VCC
  N9: R1.Pin_0, R2.Pin_1
  N10: R2.Pin_0, Int1.pin1
  N11: Composant3.E+, Load_Cell1.wire1
  N12: Composant3.E-, Load_Cell1.wire3
  N13: Composant3.A+, Load_Cell1.wire2
  N14: Composant3.A-, Load_Cell1.wire4
  N15: R3.Pin_1, LED1.cathode

notes:
  R = 124 Ohm
  SEN0291
  SCL
  SDA
  Panneau Solaire
  Interrupteur
  Carte LiPo Rider Pro 106990008
  LED
  Arduino MKRWan 1310
  DHT22
  DS18B20
  HX711
  R = 1k Ohm
  1ICP5/45/46
  3.9Wh,
  1050mAh,
  3.7V

custom parts:
  Arduino MKR WAN 1310: The Arduino MKR WAN 1310 board provides a practical and cost effective solution to add LoRa® connectivity to projects requiring low power. This open source board can be connected to: the Arduino IoT Cloud, your own LoRa® network using the Arduino LoRa® PRO Gateway, existing LoRaWAN™ infrastructure like The Things Network, or even other boards using the direct connectivity mode.
  Interrupteur à levier - 2 pins: Interrupteur à levier 2 bornes
  DHT11 Humitidy and Temperature Sensor: DHT11 Humidity and Temperature Sensor
  HX711 Weighing Sensor Module: HX711 is a precision 24-bit analog-to-digital converter (ADC) designed for weigh scales and industrial control applications to interface directly with a bridge sensor.
  Load Cell - Red/white/black/green: A rectangle load cell/weighting pressure Sensor with four wires - Red, white, black, green. Normally corresponding with E+, E-, A+, A- respectively.
